// Logisim project procesador_monociclo.circ as structural Verilog: 1 circuit, main circuit main
module main (
  input  RST,
  output [31:0] PC,
  output [31:0] INSTR,
  output [31:0] A,
  output [31:0] B,
  output [31:0] ALU,
  output [31:0] W,
  output [31:0] MEM,
  output [31:0] R0,
  output [31:0] R1,
  output [31:0] R2,
  output [31:0] R3,
  output [31:0] R4,
  output [31:0] R5,
  output [31:0] R6,
  output [31:0] R7,
  output [31:0] R8,
  output [31:0] R9,
  output [31:0] R10,
  output [31:0] R11,
  output [31:0] R12,
  output [31:0] R13,
  output [31:0] R14,
  output [31:0] R15,
  output [31:0] R16,
  output [31:0] R17,
  output [31:0] R18,
  output [31:0] R19,
  output [31:0] R20,
  output [31:0] R21,
  output [31:0] R22,
  output [31:0] R23,
  output [31:0] R24,
  output [31:0] R25,
  output [31:0] R26,
  output [31:0] R27,
  output [31:0] R28,
  output [31:0] R29,
  output [31:0] R30,
  output [31:0] R31
);

  wire ALUSrc, Branch, Branch_AND_Zero_out, clock_1_out, comparator_1_lt, Decodificador_out1,
       Decodificador_out2, Decodificador_out3, Decodificador_out4, Decodificador_out5, Decodificador_out6,
       Decodificador_out7, Decodificador_out8, Decodificador_out9, Decodificador_out10, Decodificador_out11,
       Decodificador_out12, Decodificador_out13, Decodificador_out14, Decodificador_out15,
       Decodificador_out16, Decodificador_out17, Decodificador_out18, Decodificador_out19,
       Decodificador_out20, Decodificador_out21, Decodificador_out22, Decodificador_out23,
       Decodificador_out24, Decodificador_out25, Decodificador_out26, Decodificador_out27,
       Decodificador_out28, Decodificador_out29, Decodificador_out30, Decodificador_out31, one, RegWrite,
       undriven, undriven_2, undriven_3, undriven_34, undriven_35, undriven_36, undriven_37, undriven_38,
       undriven_39, undriven_40, undriven_41, undriven_42, undriven_43, undriven_44, undriven_45,
       undriven_46, undriven_47, undriven_48, undriven_49, undriven_50, undriven_51, undriven_52,
       undriven_53, undriven_54, undriven_55, undriven_56, undriven_57, undriven_58, undriven_59,
       undriven_60, undriven_61, undriven_62, undriven_63, undriven_64, undriven_65, undriven_66,
       undriven_67, undriven_68, undriven_69, undriven_70, undriven_71, undriven_72, undriven_73,
       undriven_74, undriven_75, undriven_76, undriven_77, undriven_78, undriven_79, undriven_80,
       undriven_81, undriven_82, undriven_83, undriven_84, undriven_85, undriven_86, undriven_87,
       undriven_88, undriven_89, undriven_90, undriven_91, undriven_92, undriven_93, undriven_94,
       undriven_95, zero_flag;
  wire [2:0] Control_ALU_data;
  wire [4:0] Registro_destino_out;
  wire [7:0] bitselector_1_out;
  wire [7:6] Unidad_de_control_data;
  wire [15:0] Unidad_de_control_data_2;
  wire [31:0] adder_1_out, and_1_out, bit_extender_1_out, bit_extender_2_out, Desplaza_offset_out, imm32,
       jump_addr, lb_val, MemtoReg_out, Mux_ALUSrc_out, nor_1_out, or_1_out, pc4, PC_31_28_out, pc_next,
       PC_relativo_out, PC_secuencial___branch_out, shifter_1_out, subtractor_1_out, undriven_4, undriven_5,
       undriven_6, undriven_7, undriven_8, undriven_9, undriven_10, undriven_11, undriven_12, undriven_13,
       undriven_14, undriven_15, undriven_16, undriven_17, undriven_18, undriven_19, undriven_20,
       undriven_21, undriven_22, undriven_23, undriven_24, undriven_25, undriven_26, undriven_27,
       undriven_28, undriven_29, undriven_30, undriven_31, undriven_32, undriven_33;

  Clock clock_1 (.out(clock_1_out));
  Decoder #(.select(5), .enable("true")) Decodificador (
    .out0(one), .out1(Decodificador_out1), .out2(Decodificador_out2), .out3(Decodificador_out3),
    .out4(Decodificador_out4), .out5(Decodificador_out5), .out6(Decodificador_out6),
    .out7(Decodificador_out7), .out8(Decodificador_out8), .out9(Decodificador_out9),
    .out10(Decodificador_out10), .out11(Decodificador_out11), .out12(Decodificador_out12),
    .out13(Decodificador_out13), .out14(Decodificador_out14), .out15(Decodificador_out15),
    .out16(Decodificador_out16), .out17(Decodificador_out17), .out18(Decodificador_out18),
    .out19(Decodificador_out19), .out20(Decodificador_out20), .out21(Decodificador_out21),
    .out22(Decodificador_out22), .out23(Decodificador_out23), .out24(Decodificador_out24),
    .out25(Decodificador_out25), .out26(Decodificador_out26), .out27(Decodificador_out27),
    .out28(Decodificador_out28), .out29(Decodificador_out29), .out30(Decodificador_out30),
    .out31(Decodificador_out31), .sel(Registro_destino_out), .en(RegWrite));
  Register #(.width(32), .trigger("rising")) Registro_PC (
    .D(pc_next), .en(one), .Q(PC), .clk(undriven_2), .clr(undriven));
  Register #(.width(32), .trigger("rising")) u_r0 (.D({32{1'b0}}), .en(one), .Q(R0), .clk(clock_1_out), .clr(RST));
  Register #(.width(32), .trigger("rising")) u_r1 (
    .D(W), .en(Decodificador_out1), .Q(R1), .clk(undriven_34), .clr(undriven_65));
  Register #(.width(32), .trigger("rising")) u_r2 (
    .D(undriven_4), .en(Decodificador_out2), .Q(R2), .clk(undriven_35), .clr(undriven_66));
  Register #(.width(32), .trigger("rising")) u_r3 (
    .D(undriven_5), .en(Decodificador_out3), .Q(R3), .clk(undriven_36), .clr(undriven_67));
  Register #(.width(32), .trigger("rising")) u_r4 (
    .D(undriven_6), .en(Decodificador_out4), .Q(R4), .clk(undriven_37), .clr(undriven_68));
  Register #(.width(32), .trigger("rising")) u_r5 (
    .D(undriven_7), .en(Decodificador_out5), .Q(R5), .clk(undriven_38), .clr(undriven_69));
  Register #(.width(32), .trigger("rising")) u_r6 (
    .D(undriven_8), .en(Decodificador_out6), .Q(R6), .clk(undriven_39), .clr(undriven_70));
  Register #(.width(32), .trigger("rising")) u_r7 (
    .D(undriven_9), .en(Decodificador_out7), .Q(R7), .clk(undriven_40), .clr(undriven_71));
  Register #(.width(32), .trigger("rising")) u_r8 (
    .D(undriven_10), .en(Decodificador_out8), .Q(R8), .clk(undriven_41), .clr(undriven_72));
  Register #(.width(32), .trigger("rising")) u_r9 (
    .D(undriven_11), .en(Decodificador_out9), .Q(R9), .clk(undriven_42), .clr(undriven_73));
  Register #(.width(32), .trigger("rising")) u_r10 (
    .D(undriven_12), .en(Decodificador_out10), .Q(R10), .clk(undriven_43), .clr(undriven_74));
  Register #(.width(32), .trigger("rising")) u_r11 (
    .D(undriven_13), .en(Decodificador_out11), .Q(R11), .clk(undriven_44), .clr(undriven_75));
  Register #(.width(32), .trigger("rising")) u_r12 (
    .D(undriven_14), .en(Decodificador_out12), .Q(R12), .clk(undriven_45), .clr(undriven_76));
  Register #(.width(32), .trigger("rising")) u_r13 (
    .D(undriven_15), .en(Decodificador_out13), .Q(R13), .clk(undriven_46), .clr(undriven_77));
  Register #(.width(32), .trigger("rising")) u_r14 (
    .D(undriven_16), .en(Decodificador_out14), .Q(R14), .clk(undriven_47), .clr(undriven_78));
  Register #(.width(32), .trigger("rising")) u_r15 (
    .D(undriven_17), .en(Decodificador_out15), .Q(R15), .clk(undriven_48), .clr(undriven_79));
  Register #(.width(32), .trigger("rising")) u_r16 (
    .D(undriven_18), .en(Decodificador_out16), .Q(R16), .clk(undriven_49), .clr(undriven_80));
  Register #(.width(32), .trigger("rising")) u_r17 (
    .D(undriven_19), .en(Decodificador_out17), .Q(R17), .clk(undriven_50), .clr(undriven_81));
  Register #(.width(32), .trigger("rising")) u_r18 (
    .D(undriven_20), .en(Decodificador_out18), .Q(R18), .clk(undriven_51), .clr(undriven_82));
  Register #(.width(32), .trigger("rising")) u_r19 (
    .D(undriven_21), .en(Decodificador_out19), .Q(R19), .clk(undriven_52), .clr(undriven_83));
  Register #(.width(32), .trigger("rising")) u_r20 (
    .D(undriven_22), .en(Decodificador_out20), .Q(R20), .clk(undriven_53), .clr(undriven_84));
  Register #(.width(32), .trigger("rising")) u_r21 (
    .D(undriven_23), .en(Decodificador_out21), .Q(R21), .clk(undriven_54), .clr(undriven_85));
  Register #(.width(32), .trigger("rising")) u_r22 (
    .D(undriven_24), .en(Decodificador_out22), .Q(R22), .clk(undriven_55), .clr(undriven_86));
  Register #(.width(32), .trigger("rising")) u_r23 (
    .D(undriven_25), .en(Decodificador_out23), .Q(R23), .clk(undriven_56), .clr(undriven_87));
  Register #(.width(32), .trigger("rising")) u_r24 (
    .D(undriven_26), .en(Decodificador_out24), .Q(R24), .clk(undriven_57), .clr(undriven_88));
  Register #(.width(32), .trigger("rising")) u_r25 (
    .D(undriven_27), .en(Decodificador_out25), .Q(R25), .clk(undriven_58), .clr(undriven_89));
  Register #(.width(32), .trigger("rising")) u_r26 (
    .D(undriven_28), .en(Decodificador_out26), .Q(R26), .clk(undriven_59), .clr(undriven_90));
  Register #(.width(32), .trigger("rising")) u_r27 (
    .D(undriven_29), .en(Decodificador_out27), .Q(R27), .clk(undriven_60), .clr(undriven_91));
  Register #(.width(32), .trigger("rising")) u_r28 (
    .D(undriven_30), .en(Decodificador_out28), .Q(R28), .clk(undriven_61), .clr(undriven_92));
  Register #(.width(32), .trigger("rising")) u_r29 (
    .D(undriven_31), .en(Decodificador_out29), .Q(R29), .clk(undriven_62), .clr(undriven_93));
  Register #(.width(32), .trigger("rising")) u_r30 (
    .D(undriven_32), .en(Decodificador_out30), .Q(R30), .clk(undriven_63), .clr(undriven_94));
  Register #(.width(32), .trigger("rising")) u_r31 (
    .D(undriven_33), .en(Decodificador_out31), .Q(R31), .clk(undriven_64), .clr(undriven_95));
  Adder #(.width(32)) PC_4 (.a(PC), .b(32'h4), .out(pc4), .cin(1'b0));  // open: cout
  ROM #(.addrWidth(12), .dataWidth(32)) Memoria_de_instrucciones (.addr(PC[11:0]), .data(INSTR));
  Multiplexer #(.select(5), .width(32)) Mux_A__rs (
    .in0(R0), .in1(R1), .in2(R2), .in3(R3), .in4(R4), .in5(R5), .in6(R6), .in7(R7), .in8(R8), .in9(R9),
    .in10(R10), .in11(R11), .in12(R12), .in13(R13), .in14(R14), .in15(R15), .in16(R16), .in17(R17),
    .in18(R18), .in19(R19), .in20(R20), .in21(R21), .in22(R22), .in23(R23), .in24(R24), .in25(R25),
    .in26(R26), .in27(R27), .in28(R28), .in29(R29), .in30(R30), .in31(R31), .out(A), .sel(INSTR[25:21]));
  Multiplexer #(.select(5), .width(32)) Mux_B__rt (
    .in0(R0), .in1(R1), .in2(R2), .in3(R3), .in4(R4), .in5(R5), .in6(R6), .in7(R7), .in8(R8), .in9(R9),
    .in10(R10), .in11(R11), .in12(R12), .in13(R13), .in14(R14), .in15(R15), .in16(R16), .in17(R17),
    .in18(R18), .in19(R19), .in20(R20), .in21(R21), .in22(R22), .in23(R23), .in24(R24), .in25(R25),
    .in26(R26), .in27(R27), .in28(R28), .in29(R29), .in30(R30), .in31(R31), .out(B), .sel(INSTR[20:16]));
  assign imm32 = {{16{INSTR[15]}}, INSTR[15:0]};  // Bit_Extender Extensor_de_signo
  and Branch_AND_Zero (Branch_AND_Zero_out, Branch, zero_flag);
  Shifter #(.width(32), .shift("ll")) Desplaza_offset (.in(imm32), .\dist (5'b00010), .out(Desplaza_offset_out));
  assign bit_extender_1_out = {{6{1'b0}}, INSTR[25:0]};  // Bit_Extender bit_extender_1
  ROM #(.addrWidth(12), .dataWidth(16)) Unidad_de_control (
    .addr({INSTR[31:26], INSTR[5:0]}),
    .data({Unidad_de_control_data_2[15:13], Unidad_de_control_data, Unidad_de_control_data_2[10:8], Branch, Unidad_de_control_data_2[6:5], RegWrite, Unidad_de_control_data_2[3:2], ALUSrc, Unidad_de_control_data_2[0]}));
  ROM #(.addrWidth(8), .dataWidth(3)) Control_ALU (
    .addr({Unidad_de_control_data, INSTR[5:0]}), .data(Control_ALU_data));
  Multiplexer #(.select(1), .width(32)) Mux_ALUSrc (.in0(B), .in1(imm32), .out(Mux_ALUSrc_out), .sel(ALUSrc));
  Adder #(.width(32)) PC_relativo (.a(pc4), .b(Desplaza_offset_out), .out(PC_relativo_out), .cin(1'b0));  // open: cout
  Shifter #(.width(32), .shift("ll")) shifter_1 (.in(bit_extender_1_out), .\dist (5'b00010), .out(shifter_1_out));
  Multiplexer #(.select(1), .width(32)) PC_secuencial___branch (
    .in0(pc4), .in1(PC_relativo_out), .out(PC_secuencial___branch_out), .sel(Branch_AND_Zero_out));
  assign PC_31_28_out = pc4 & 32'hf0000000;  // AND_Gate PC_31_28, 32 bits wide
  assign and_1_out = A & Mux_ALUSrc_out;  // AND_Gate and_1, 32 bits wide
  assign or_1_out = A | Mux_ALUSrc_out;  // OR_Gate or_1, 32 bits wide
  assign nor_1_out = ~(A | Mux_ALUSrc_out);  // NOR_Gate nor_1, 32 bits wide
  Adder #(.width(32)) adder_1 (.a(A), .b(Mux_ALUSrc_out), .out(adder_1_out), .cin(1'b0));  // open: cout
  Subtractor #(.width(32)) subtractor_1 (.a(A), .b(Mux_ALUSrc_out), .out(subtractor_1_out), .bin(1'b0));  // open: bout
  Comparator #(.width(32), .mode("twosComplement")) comparator_1 (
    .a(A), .b(Mux_ALUSrc_out), .lt(comparator_1_lt));  // open: gt, eq
  Multiplexer #(.select(2), .width(32)) Proximo_PC (
    .in0(PC_secuencial___branch_out), .in1(jump_addr), .in2(A), .in3(A), .out(pc_next),
    .sel({Unidad_de_control_data_2[10], Unidad_de_control_data_2[8]}));
  assign jump_addr = shifter_1_out | PC_31_28_out;  // OR_Gate Direccion_de_salto, 32 bits wide
  assign bit_extender_2_out = {{31{1'b0}}, comparator_1_lt};  // Bit_Extender bit_extender_2
  Multiplexer #(.select(3), .width(32)) Resultado_ALU (
    .in0(adder_1_out), .in1(subtractor_1_out), .in2(and_1_out), .in3(or_1_out), .in4(nor_1_out),
    .in5(bit_extender_2_out), .in6({32{1'b0}}), .in7({32{1'b0}}), .out(ALU), .sel(Control_ALU_data));
  Multiplexer #(.select(2), .width(5)) Registro_destino (
    .in0(INSTR[20:16]), .in1(INSTR[15:11]), .in2({5{1'b1}}), .in3({5{1'b1}}), .out(Registro_destino_out),
    .sel({Unidad_de_control_data_2[9], Unidad_de_control_data_2[0]}));
  Comparator #(.width(32), .mode("unsigned")) Zero (.a(ALU), .b({32{1'b0}}), .eq(zero_flag));  // open: gt, lt
  RAM #(.addrWidth(12), .dataWidth(32), .enables("byte"), .databus("bibus"), .asyncread("true"), .trigger("rising"), .byteenables("NobyteEnables"), .\type ("volatile"), .clearpin("false"), .line("single"), .misaligned("false")) Memoria_de_datos (
    .addr(ALU[13:2]), .we(Unidad_de_control_data_2[6]), .oe(Unidad_de_control_data_2[5]), .clk(undriven_3),
    .din(B), .dout(MEM));
  Multiplexer #(.select(2), .width(32)) MemtoReg (
    .in0(ALU), .in1(MEM), .in2(lb_val), .in3(pc4), .out(MemtoReg_out), .sel(Unidad_de_control_data_2[3:2]));
  BitSelector #(.width(32), .group(8)) bitselector_1 (.in(MEM), .out(bitselector_1_out), .sel(ALU[1:0]));
  assign lb_val = {{24{bitselector_1_out[7]}}, bitselector_1_out};  // Bit_Extender Extension_LB
  // also tied to VCC on the sheet: one

  // Other names for the same wires on the sheet: a_val[31:0] = A; alu_res[31:0] = ALU; byte_off[1:0] = ALU[1:0];
  //   b_val[31:0] = B; rt[4:0] = INSTR[20:16]; rs[4:0] = INSTR[25:21]; mem_rdata[31:0] = MEM; wr_data[31:0] = W

  // Notes on the sheet:
  //   contents of Memoria_de_instrucciones (hex, n*v repeats v):
  //   20080200 0 0 0 2009020a 0 0 0 ad090000 0 0 0 81040000 0 0 0 20050100 0 0 0 c000012 0 0 0 20060300 0
  //   0 0 acc20000 0 0 0 20050100 0 0 0 c000036 0 0 0 acc20004 0 0 0 acc30008 0 0 0 8cd30000 0 0 0
  //   8cd40004 0 0 0 8cd50008 0 0 0 20080120 0 0 0 8d160004 0 0 0 8000011 0 0 0 23bdfff4 0 0 0 afbf0008 0
  //   0 0 afb10004 0 0 0 afb20000 0 0 0 20110000 0 0 0 20120001 0 0 0 20080000 0 0 0 a05820 0 0 0 104482a
  //   0 0 0 11200014 0 0 0 1100000a 0 0 0 200a0001 0 0 0 110a000c 0 0 0 2525020 0 0 0 1515020 0 0 0
  //   2408820 0 0 0 1409020 0 0 0 ad6a0000 0 0 0 216b0004 0 0 0 21080001 0 0 0 800001a 0 0 0 ad600000 0 0
  //   0 216b0004 0 0 0 21080001 0 0 0 800001a 0 0 0 200a0001 0 0 0 ad6a0000 0 0 0 216b0004 0 0 0 21080001
  //   0 0 0 800001a 0 0 0 2401020 0 0 0 8fbf0008 0 0 0 8fb10004 0 0 0 8fb20000 0 0 0 23bd000c 0 0 0
  //   3e00008 0 0 0 23bdfffc 0 0 0 afbf0000 0 0 0 20020000 0 0 0 20030000 0 0 0 20080000 0 0 0 a05820 0 0
  //   0 104482a 0 0 0 11200006 0 0 0 816a0000 0 0 0 4a1020 0 0 0 20630001 0 0 0 216b0004 0 0 0 21080001 0
  //   0 0 800003c 0 0 0 8fbf0000 0 0 0 23bd0004 0 0 0 3e00008 3815*0
  //   contents of Unidad_de_control (hex, n*v repeats v):
  //   8*1011 400 55*1011 64*0 64*100 64*31c 64*880 192*0 64*12 1472*0 64*3a 128*0 64*36 448*0 64*42 1280*0
  //   contents of Control_ALU (hex, n*v repeats v):
  //   64*0 64*1 34*0 1 0 2 3 0 4 0 0 5 85*0
endmodule
